# Fritzing sketch X-Mas-Calendard (saved by Fritzing 0.9.10b)
breadboards: 1

parts:
  Bauteil1 = Arduino Nano (Rev3.0)
  DFRobot_DFPlayer_Mini1 = DFRobot DFPlayer Mini [part_number=DFR0299]
  Bauteil3 = RFID-RC522-v2
  SP1 = SPEAKER [package=pcb_mount_speaker]
  R1 = Resistor [tolerance=±2% power=0.25 resistance=1k package=THT]
  OLED1 = OLED 128x64 I2C Monochrome Display GND-VDD

nets:
  N1: Bauteil1.D2, DFRobot_DFPlayer_Mini1.TX
  N2: Bauteil1.D3, R1.Pin_0
  N3: Bauteil1.D4, DFRobot_DFPlayer_Mini1.BUSY
  N4: Bauteil1.D9, Bauteil3.RST
  N5: Bauteil1.D10, Bauteil3.SDA
  N6: Bauteil1.D11/MOSI, Bauteil3.MOSI
  N7: Bauteil1.D12/MISO, Bauteil3.MISO
  5V: Bauteil1.5V, DFRobot_DFPlayer_Mini1.VCC, DFRobot_DFPlayer_Mini1.GND-1, DFRobot_DFPlayer_Mini1.GND-2
  N8: Bauteil1.A5, OLED1.SCK
  N9: Bauteil1.A4, OLED1.SDA
  3V3: Bauteil1.3V3, Bauteil3.3.3V
  N10: Bauteil1.D13/SCK, Bauteil3.SCK
  N11: DFRobot_DFPlayer_Mini1.RX, R1.Pin_1
  N12: DFRobot_DFPlayer_Mini1.SPK_1, SP1.-
  N13: DFRobot_DFPlayer_Mini1.SPK_2, SP1.+
  GND: Bauteil3.GND, OLED1.GND

custom parts:
  RFID-RC522-v2: A simple China made RFID-RC522 Reader; do check the pin labels, as this is a MFRC522 based clone.
  OLED 128x64 I2C Monochrome Display GND-VDD: OLED 128x64 I2C Monochrome Display. Note: there are two variants of this part, this one is the GND VDD SCK SDA variant. The other is VDD GND SCK SDA. Make sure you select the part that matches your module as using the incorrect part will probably destroy your module! In addition the mounting holes are marked on silkscreen but not by default drilled. If you want drilled mounting holes, copy a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
